# Fritzing sketch deviceSketch (saved by Fritzing 0.9.3b)

parts:
  WeMos_D1_Mini1 = WeMos D1 Mini
  KY-1 = Keyes Relay [package=THT]
  U1 = mystery part, 4 pins [chip_label=Plug]
  LED1 = LED - 5mm [color="Red (633nm)" package="5 mm [THT]"]
  M1 = DC Motor

nets:
  N1: WeMos_D1_Mini1.5V, KY-1.power
  N2: WeMos_D1_Mini1.D0, WeMos_D1_Mini1.RST
  N3: WeMos_D1_Mini1.D1, KY-1.signal
  N4: WeMos_D1_Mini1.D4, LED1.anode
  N5: WeMos_D1_Mini1.G, KY-1.ground, LED1.cathode
  N6: KY-1.C, U1.pin1
  N7: KY-1.NO, M1.pin_2
  N8: U1.pin2, M1.pin_1

custom parts:
  Keyes Relay: The Keyes 5V relay module is suitable for SCM development, home appliance control. It uses a 5V~12V TIL control signal which can control DC / AC signal.
